# Fritzing sketch PaperPlane (saved by Fritzing 0.9.5d)
breadboards: 1

parts:
  元件1 = Arduino Nano (Rev3.0)
  J1 = Basic Servo
  M1 = DC Motor
  J2 = Basic Servo
  元件2 = Bluetooth HC-05 Macho
  U1 = LIPO-110mAh [package=lipo-110]
  Mod1 = Talon SRX

nets:
  N1: 元件1.D1/TX, 元件2.TXD
  N2: 元件1.D0/RX, 元件2.RXD
  GND: 元件1.GND, J1.gnd, J2.gnd, 元件2.GND, U1.-, Mod1.GND, Mod1.Pin_10
  N3: 元件1.D2, J1.pulse
  N4: 元件1.D3, J2.pulse
  N5: 元件1.D10, Mod1.Pin_3
  N6: 元件1.VIN, Mod1.Pin_2
  3V3: 元件1.3V3, 元件2.VCC
  VCC: J1.vcc, J2.vcc, U1.+, Mod1.V+
  N7: M1.pin_1, Mod1.M-
  N8: M1.pin_2, Mod1.M+
